// Logisim project FinalProject.circ as structural Verilog: 15 circuits, main circuit main
module main (
);

  wire and_1_out, and_2_out, Clear, clock_1_out, CR, d_ff_1_q, Enter, Halt, IncPC, InputWait, K0_out, K1_out,
       K2_out, K3_out, K4_out, K5_out, K6_out, K7_out, K8_out, K9_out, KA_out, KB_out, KC_out, KD_out,
       KE_out, KF_out, Lalt, MR, MW, not_1_out, not_2_out, not_3_out, not_4_out, not_5_out, or_1_out,
       or_2_out, priority_encoder_1_gs;
  wire [1:0] A0A1, AOA1;
  wire [2:0] P012, P345;
  wire [3:0] multiplexer_3_out, multiplexer_3_out_2, multiplexer_3_out_3, multiplexer_3_out_4,
       priority_encoder_1_out;
  wire [7:0] DMX, InReg, Keyboard, RC;
  wire [11:0] MAR;
  wire [15:0] AC, AluOut, IR, MBR, MEM, multiplexer_1_out, multiplexer_2_out;
  wire [43:28] MPX1;
  wire [47:32] MPX2;

  not not_1 (not_1_out, Enter);
  and and_1 (and_1_out, InputWait, not_1_out);
  or or_1 (or_1_out, Halt, and_1_out);
  not not_2 (not_2_out, or_1_out);
  and and_2 (and_2_out, clock_1_out, not_2_out);
  or or_2 (or_2_out, CR, InputWait);
  Clock clock_1 (.out(clock_1_out));
  D_Flip_Flop d_ff_1 (.D(or_2_out), .clk(clock_1_out), .Q(d_ff_1_q), .reset(not_3_out));  // open: Qn, preset
  not not_3 (not_3_out, d_ff_1_q);
  Demultiplexer #(.select(3)) demultiplexer_1 (
    .out0(DMX[0]), .out1(DMX[1]), .out2(DMX[2]), .out3(DMX[3]), .out4(DMX[4]), .out5(DMX[5]), .out6(DMX[6]),
    .out7(DMX[7]), .in(1'b1), .sel(P345));
  RAM #(.addrWidth(12), .dataWidth(16)) ram_1 (
    .addr(MAR), .we(MW), .oe(MR), .clk(clock_1_out),
    .din({multiplexer_3_out_4, multiplexer_3_out_3, multiplexer_3_out_2, multiplexer_3_out}), .dout(MEM));
  Multiplexer #(.width(16)) multiplexer_1 (
    .in0({multiplexer_3_out_4, multiplexer_3_out_3, multiplexer_3_out_2, multiplexer_3_out}), .in1(AC),
    .out(multiplexer_1_out), .sel(Lalt));
  Multiplexer #(.width(16)) multiplexer_2 (
    .in0({multiplexer_3_out_4, multiplexer_3_out_3, multiplexer_3_out_2, multiplexer_3_out}), .in1(AluOut),
    .out(multiplexer_2_out), .sel(Lalt));
  Register #(.trigger("falling"), .width(12)) u_MAR (
    .D({multiplexer_3_out_3, multiplexer_3_out_2, multiplexer_3_out}), .en(DMX[1]), .clk(clock_1_out), .Q(MAR));  // open: clr
  Counter #(.max('hfff), .width(12)) PC (
    .load(DMX[2]), .D({multiplexer_3_out_3, multiplexer_3_out_2, multiplexer_3_out}), .count(not_4_out),
    .Q(MPX1[43:32]), .up(1'b1), .clk(not_5_out));  // open: carry, clr
  not not_4 (not_4_out, DMX[2]);
  not not_5 (not_5_out, IncPC);
  Register #(.trigger("falling"), .width(16)) u_MBR (
    .D(multiplexer_1_out), .en(DMX[3]), .clk(clock_1_out), .Q(MBR));  // open: clr
  Register #(.trigger("falling"), .width(16)) u_AC (
    .D(multiplexer_2_out), .en(DMX[4]), .clk(clock_1_out), .Q(AC), .clr(Clear));
  Register #(.trigger("falling")) u_InReg (.D(Keyboard), .en(DMX[5]), .clk(clock_1_out), .Q(InReg));  // open: clr
  Register #(.trigger("falling")) OutReg (
    .D({multiplexer_3_out_2, multiplexer_3_out}), .en(DMX[6]), .clk(clock_1_out), .Q(MPX2[39:32]));  // open: clr
  Register #(.trigger("falling"), .width(16)) u_IR (
    .D({multiplexer_3_out_4, multiplexer_3_out_3, multiplexer_3_out_2, multiplexer_3_out}), .en(DMX[7]),
    .clk(clock_1_out), .Q(IR));  // open: clr
  RingCounter ringcounter_1 (
    .Clk(and_2_out), .Cr(d_ff_1_q), .T0(RC[0]), .T1(RC[1]), .T2(RC[2]), .T3(RC[3]), .T4(RC[4]), .T5(RC[5]),
    .T6(RC[6]), .T7(RC[7]));
  Multiplexer #(.select(3), .width(16)) multiplexer_3 (
    .in0(MEM), .in1({MPX1[31:28], MAR}), .in2({4'b0000, MPX1[43:32]}), .in3(MBR), .in4(AC),
    .in5({{8{1'b0}}, InReg}), .in6(MPX2), .in7(IR),
    .out({multiplexer_3_out_4, multiplexer_3_out_3, multiplexer_3_out_2, multiplexer_3_out}), .sel(P012));
  ALU alu_1 (.MBR(MBR), .AC(AC), .A1A0(A0A1), .ALUoutput(AluOut));
  Hex_Digit_Display hex_digit_display_1 (.value(multiplexer_3_out_4));  // open: dp
  Hex_Digit_Display hex_digit_display_2 (.value(multiplexer_3_out_3));  // open: dp
  ControlUnit controlunit_1 (
    .IR(IR), .RingCounter(RC), .AC(AC), .P0Signal(P012[0]), .P1Signal(P012[1]), .P2Signal(P012[2]),
    .P3Signal(P345[0]), .P4Signal(P345[1]), .P5Signal(P345[2]), .MrSignal(MR), .MwSignal(MW), .CrSignal(CR),
    .LaltSignal(Lalt), .IncPCsignal(IncPC), .A0Signal(AOA1[0]), .A1Signal(AOA1[1]), .HaltSignal(Halt),
    .InputWait(InputWait), .ClearSignal(Clear));
  Hex_Digit_Display hex_digit_display_3 (.value(multiplexer_3_out_2));  // open: dp
  Hex_Digit_Display hex_digit_display_4 (.value(multiplexer_3_out));  // open: dp
  Button K0 (.out(K0_out));
  Button K4 (.out(K4_out));
  Button K8 (.out(K8_out));
  Button KC (.out(KC_out));
  Button K1 (.out(K1_out));
  Button K2 (.out(K2_out));
  Button K5 (.out(K5_out));
  Button K6 (.out(K6_out));
  Button K9 (.out(K9_out));
  Button KA (.out(KA_out));
  Button KD (.out(KD_out));
  Button KE (.out(KE_out));
  Button u_Enter (.out(Enter));
  Button K3 (.out(K3_out));
  Button K7 (.out(K7_out));
  Button KB (.out(KB_out));
  Button KF (.out(KF_out));
  Priority_Encoder #(.select(4)) priority_encoder_1 (
    .in0(K0_out), .in1(K1_out), .in2(K2_out), .in3(K3_out), .in4(K4_out), .in5(K5_out), .in6(K6_out),
    .in7(K7_out), .in8(K8_out), .in9(K9_out), .in10(KA_out), .in11(KB_out), .in12(KC_out), .in13(KD_out),
    .in14(KE_out), .in15(KF_out), .out(priority_encoder_1_out), .gs(priority_encoder_1_gs));  // open: en_out, en_in
  // Shift_Register #(.length(2), .width(4)) shift_register_1: pin names not known; wires that end beside it: priority_encoder_1_gs, priority_encoder_1_out, Keyboard[3:0], Keyboard[7:4]
  Hex_Digit_Display hex_digit_display_5 (.value(MAR[11:8]));  // open: dp
  Hex_Digit_Display hex_digit_display_6 (.value(MBR[15:12]));  // open: dp
  Hex_Digit_Display hex_digit_display_7 (.value(IR[15:12]));  // open: dp
  Hex_Digit_Display hex_digit_display_8 (.value(IR[11:8]));  // open: dp
  Hex_Digit_Display hex_digit_display_9 (.value(MAR[7:4]));  // open: dp
  Hex_Digit_Display hex_digit_display_10 (.value(MAR[3:0]));  // open: dp
  Hex_Digit_Display hex_digit_display_11 (.value(MBR[11:8]));  // open: dp
  Hex_Digit_Display hex_digit_display_12 (.value(MBR[7:4]));  // open: dp
  Hex_Digit_Display hex_digit_display_13 (.value(IR[7:4]));  // open: dp
  Hex_Digit_Display hex_digit_display_14 (.value(IR[3:0]));  // open: dp
  Hex_Digit_Display hex_digit_display_15 (.value(Keyboard[7:4]));  // open: dp
  Hex_Digit_Display hex_digit_display_16 (.value(MBR[3:0]));  // open: dp
  Hex_Digit_Display hex_digit_display_17 (.value(Keyboard[3:0]));  // open: dp
  Hex_Digit_Display hex_digit_display_18 (.value(MPX1[43:40]));  // open: dp
  Hex_Digit_Display hex_digit_display_19 (.value(AC[15:12]));  // open: dp
  Hex_Digit_Display hex_digit_display_20 (.value(AluOut[15:12]));  // open: dp
  Hex_Digit_Display hex_digit_display_21 (.value(MPX1[39:36]));  // open: dp
  Hex_Digit_Display hex_digit_display_22 (.value(MPX1[35:32]));  // open: dp
  Hex_Digit_Display hex_digit_display_23 (.value(AC[11:8]));  // open: dp
  Hex_Digit_Display hex_digit_display_24 (.value(AC[7:4]));  // open: dp
  Hex_Digit_Display hex_digit_display_25 (.value(AluOut[11:8]));  // open: dp
  Hex_Digit_Display hex_digit_display_26 (.value(AluOut[7:4]));  // open: dp
  Hex_Digit_Display hex_digit_display_27 (.value(AC[3:0]));  // open: dp
  Hex_Digit_Display hex_digit_display_28 (.value(AluOut[3:0]));  // open: dp

  // Other names for the same wires on the sheet: MPX1 (some bits) = {MBR, MAR, MEM}; PC[11:0] = MPX1[43:32];
  //   MPX2 (some bits) = {IR, InReg, AC}; OutReg[7:0] = MPX2[39:32]
endmodule

module ALU (
  input  [15:0] MBR,
  input  [15:0] AC,
  input  [1:0] A1A0,
  output [15:0] ALUoutput
);

  wire [15:0] adder_1_out, subtractor_1_out;

  Adder #(.width(16)) adder_1 (.a(AC), .b(MBR), .out(adder_1_out));  // open: cin, cout
  Subtractor #(.width(16)) subtractor_1 (.a(AC), .b(MBR), .out(subtractor_1_out));  // open: bin, bout
  Multiplexer #(.select(2), .width(16)) multiplexer_1 (
    .in0({16{1'b1}}), .in1(adder_1_out), .in2(subtractor_1_out), .in3({16{1'b0}}), .out(ALUoutput), .sel(A1A0));
endmodule

module ControlUnit (
  input  [15:0] IR,
  input  [7:0] RingCounter,
  input  [15:0] AC,
  output P0Signal,
  output P1Signal,
  output P2Signal,
  output P3Signal,
  output P4Signal,
  output P5Signal,
  output MrSignal,
  output MwSignal,
  output CrSignal,
  output LaltSignal,
  output IncPCsignal,
  output A0Signal,
  output A1Signal,
  output HaltSignal,
  output InputWait,
  output ClearSignal
);

  wire addinstruction_1_a0, addinstruction_1_cr, addinstruction_1_lalt, addinstruction_1_mr,
       addinstruction_1_p0, addinstruction_1_p1, addinstruction_1_p2, addinstruction_1_p3,
       addinstruction_1_p4, addinstruction_1_p5, decoder_1_out1, decoder_1_out2, decoder_1_out3,
       decoder_1_out4, decoder_1_out5, decoder_1_out6, decoder_1_out7, decoder_1_out8, decoder_1_out9,
       decoder_1_out10, fetchcycle_1_incpc, fetchcycle_1_mr, fetchcycle_1_p1, fetchcycle_1_p3,
       fetchcycle_1_p4, fetchcycle_1_p5, inputinstruction_1_cr, inputinstruction_1_p0, inputinstruction_1_p2,
       inputinstruction_1_p3, inputinstruction_1_p5, jumpinstruction_1_cr, jumpinstruction_1_p0,
       jumpinstruction_1_p1, jumpinstruction_1_p2, jumpinstruction_1_p4, loadinstruction_1_cr,
       loadinstruction_1_mr, loadinstruction_1_p0, loadinstruction_1_p1, loadinstruction_1_p2,
       loadinstruction_1_p3, loadinstruction_1_p4, loadinstruction_1_p5, outputinstruction_1_cr,
       outputinstruction_1_p2, outputinstruction_1_p4, outputinstruction_1_p5, skipcondinstruction_1_cr,
       skipcondinstruction_1_incpc, storeinstruction_1_cr, storeinstruction_1_mw, storeinstruction_1_p0,
       storeinstruction_1_p1, storeinstruction_1_p2, storeinstruction_1_p3, storeinstruction_1_p4,
       subtinstruction_1_a1, subtinstruction_1_cr, subtinstruction_1_lalt, subtinstruction_1_mr,
       subtinstruction_1_p0, subtinstruction_1_p1, subtinstruction_1_p2, subtinstruction_1_p3,
       subtinstruction_1_p4, subtinstruction_1_p5;

  Decoder #(.select(4)) decoder_1 (
    .out1(decoder_1_out1), .out2(decoder_1_out2), .out3(decoder_1_out3), .out4(decoder_1_out4),
    .out5(decoder_1_out5), .out6(decoder_1_out6), .out7(decoder_1_out7), .out8(decoder_1_out8),
    .out9(decoder_1_out9), .out10(decoder_1_out10), .sel(IR[15:12]));  // open: out0, out11, out12, out13, out14, out15, en
  FetchCycle fetchcycle_1 (
    .RingCounter(RingCounter), .P1(fetchcycle_1_p1), .P3(fetchcycle_1_p3), .Mr(fetchcycle_1_mr),
    .P4(fetchcycle_1_p4), .P5(fetchcycle_1_p5), .IncPC(fetchcycle_1_incpc));
  LoadInstruction loadinstruction_1 (
    .RingCounter(RingCounter), .Load(decoder_1_out1), .P0(loadinstruction_1_p0), .P1(loadinstruction_1_p1),
    .P2(loadinstruction_1_p2), .P3(loadinstruction_1_p3), .Mr(loadinstruction_1_mr),
    .P4(loadinstruction_1_p4), .P5(loadinstruction_1_p5), .Cr(loadinstruction_1_cr));
  StoreInstruction storeinstruction_1 (
    .RingCounter(RingCounter), .Store(decoder_1_out2), .P0(storeinstruction_1_p0),
    .P1(storeinstruction_1_p1), .P2(storeinstruction_1_p2), .P3(storeinstruction_1_p3),
    .P4(storeinstruction_1_p4), .Mw(storeinstruction_1_mw), .Cr(storeinstruction_1_cr));
  AddInstruction addinstruction_1 (
    .RingCounter(RingCounter), .Add(decoder_1_out3), .P0(addinstruction_1_p0), .P1(addinstruction_1_p1),
    .P2(addinstruction_1_p2), .P3(addinstruction_1_p3), .Mr(addinstruction_1_mr), .P4(addinstruction_1_p4),
    .P5(addinstruction_1_p5), .Lalt(addinstruction_1_lalt), .A0(addinstruction_1_a0), .Cr(addinstruction_1_cr));
  SubtInstruction subtinstruction_1 (
    .RingCounter(RingCounter), .Subt(decoder_1_out4), .P0(subtinstruction_1_p0), .P1(subtinstruction_1_p1),
    .P2(subtinstruction_1_p2), .P3(subtinstruction_1_p3), .Mr(subtinstruction_1_mr),
    .P4(subtinstruction_1_p4), .P5(subtinstruction_1_p5), .Lalt(subtinstruction_1_lalt),
    .A1(subtinstruction_1_a1), .Cr(subtinstruction_1_cr));
  InputInstruction inputinstruction_1 (
    .RingCounter(RingCounter), .Inpt(decoder_1_out5), .P3(inputinstruction_1_p3), .InputWait(InputWait),
    .P0(inputinstruction_1_p0), .P2(inputinstruction_1_p2), .P5(inputinstruction_1_p5),
    .Cr(inputinstruction_1_cr));
  OutputInstruction outputinstruction_1 (
    .RingCounter(RingCounter), .Outpt(decoder_1_out6), .P2(outputinstruction_1_p2),
    .P4(outputinstruction_1_p4), .P5(outputinstruction_1_p5), .Cr(outputinstruction_1_cr));
  HaltInstruction haltinstruction_1 (.RingCounter(RingCounter), .Halt(decoder_1_out7), .HaltSignal(HaltSignal));
  SkipcondInstruction skipcondinstruction_1 (
    .RingCounter(RingCounter), .Skipcond(decoder_1_out8), .IR(IR), .AC(AC),
    .IncPC(skipcondinstruction_1_incpc), .Cr(skipcondinstruction_1_cr));
  JumpInstruction jumpinstruction_1 (
    .RingCounter(RingCounter), .Jump(decoder_1_out9), .P0(jumpinstruction_1_p0), .P1(jumpinstruction_1_p1),
    .P2(jumpinstruction_1_p2), .P4(jumpinstruction_1_p4), .Cr(jumpinstruction_1_cr));
  ClearInstruction clearinstruction_1 (.RingCounter(RingCounter), .Clear(decoder_1_out10), .ClearSignal(ClearSignal));
  or P0 (P0Signal, loadinstruction_1_p0, storeinstruction_1_p0, addinstruction_1_p0, subtinstruction_1_p0, inputinstruction_1_p0, skipcondinstruction_1_incpc, jumpinstruction_1_p0);
  or P1 (P1Signal, fetchcycle_1_p1, loadinstruction_1_p1, storeinstruction_1_p1, addinstruction_1_p1, subtinstruction_1_p1, skipcondinstruction_1_cr, jumpinstruction_1_p1);
  or P2 (P2Signal, loadinstruction_1_p2, storeinstruction_1_p2, addinstruction_1_p2, subtinstruction_1_p2, inputinstruction_1_p2, outputinstruction_1_p2, jumpinstruction_1_p2);
  or P3 (P3Signal, fetchcycle_1_p3, loadinstruction_1_p3, storeinstruction_1_p3, inputinstruction_1_p3, addinstruction_1_p3, subtinstruction_1_p3);
  or P4 (P4Signal, fetchcycle_1_p4, loadinstruction_1_p4, storeinstruction_1_p4, addinstruction_1_p4, subtinstruction_1_p4, outputinstruction_1_p4, jumpinstruction_1_p4);
  or P5 (P5Signal, fetchcycle_1_p5, loadinstruction_1_p5, addinstruction_1_p5, subtinstruction_1_p5, inputinstruction_1_p5, outputinstruction_1_p5);
  or Mr (MrSignal, fetchcycle_1_mr, loadinstruction_1_mr, addinstruction_1_mr, subtinstruction_1_mr);
  buf Mw (MwSignal, storeinstruction_1_mw);  // OR_Gate
  or Cr (CrSignal, loadinstruction_1_cr, storeinstruction_1_cr, addinstruction_1_cr, subtinstruction_1_cr, inputinstruction_1_cr, outputinstruction_1_cr, jumpinstruction_1_cr);
  or Lalt (LaltSignal, addinstruction_1_lalt, subtinstruction_1_lalt);
  buf IncPC (IncPCsignal, fetchcycle_1_incpc);  // OR_Gate
  buf A0 (A0Signal, addinstruction_1_a0);  // OR_Gate
  buf A1 (A1Signal, subtinstruction_1_a1);  // OR_Gate
endmodule

module FetchCycle (
  input  [7:0] RingCounter,
  output P1,
  output P3,
  output Mr,
  output P4,
  output P5,
  output IncPC
);

  or or_1 (P3, RingCounter[0], RingCounter[1]);

  assign IncPC = RingCounter[2];
  assign Mr = RingCounter[1];
  assign P1 = RingCounter[0];
  assign P4 = RingCounter[1];
  assign P5 = RingCounter[1];
endmodule

module LoadInstruction (
  input  [7:0] RingCounter,
  input  Load,
  output P0,
  output P1,
  output P2,
  output P3,
  output Mr,
  output P4,
  output P5,
  output Cr
);

  and and_1 (P2, Load, RingCounter[3]);
  and and_2 (Mr, Load, RingCounter[4]);
  and and_3 (Cr, Load, RingCounter[5]);
  or or_1 (P3, P2, Mr);
  or or_2 (P0, P2, Cr);
  or or_3 (P1, P2, Cr);

  assign P4 = Mr;
  assign P5 = Cr;
endmodule

module AddInstruction (
  input  [7:0] RingCounter,
  input  Add,
  output P0,
  output P1,
  output P2,
  output P3,
  output Mr,
  output P4,
  output P5,
  output Lalt,
  output A0,
  output Cr
);

  and and_1 (P0, Add, RingCounter[3]);
  and and_2 (Mr, Add, RingCounter[4]);
  and and_3 (A0, Add, RingCounter[5]);
  or or_1 (P3, P0, Mr);

  assign Cr = A0;
  assign Lalt = A0;
  assign P1 = P0;
  assign P2 = P0;
  assign P4 = Mr;
  assign P5 = A0;
endmodule

module StoreInstruction (
  input  [7:0] RingCounter,
  input  Store,
  output P0,
  output P1,
  output P2,
  output P3,
  output P4,
  output Mw,
  output Cr
);

  wire and_1_out;

  and and_1 (and_1_out, Store, RingCounter[3]);
  and and_2 (P4, Store, RingCounter[4]);
  and and_3 (Cr, Store, RingCounter[5]);
  or or_1 (P0, and_1_out, Cr);
  or or_2 (P1, and_1_out, Cr);
  or or_3 (P2, and_1_out, P4);
  or or_4 (P3, and_1_out, P4);

  assign Mw = Cr;
endmodule

module SubtInstruction (
  input  [7:0] RingCounter,
  input  Subt,
  output P0,
  output P1,
  output P2,
  output P3,
  output Mr,
  output P4,
  output P5,
  output Lalt,
  output A1,
  output Cr
);

  and and_1 (P0, Subt, RingCounter[3]);
  and and_2 (Mr, Subt, RingCounter[4]);
  and and_3 (A1, Subt, RingCounter[5]);
  or or_1 (P3, P0, Mr);

  assign Cr = A1;
  assign Lalt = A1;
  assign P1 = P0;
  assign P2 = P0;
  assign P4 = Mr;
  assign P5 = A1;
endmodule

module InputInstruction (
  input  [7:0] RingCounter,
  input  Inpt,
  output P3,
  output InputWait,
  output P0,
  output P2,
  output P5,
  output Cr
);

  and and_1 (InputWait, Inpt, RingCounter[3]);
  and and_2 (P3, Inpt, RingCounter[4]);
  and and_3 (Cr, Inpt, RingCounter[5]);
  or or_1 (P5, P3, Cr);

  assign P0 = Cr;
  assign P2 = Cr;
endmodule

module OutputInstruction (
  input  [7:0] RingCounter,
  input  Outpt,
  output P2,
  output P4,
  output P5,
  output Cr
);

  and and_1 (Cr, Outpt, RingCounter[3]);

  assign P2 = Cr;
  assign P4 = Cr;
  assign P5 = Cr;
endmodule

module HaltInstruction (
  input  [7:0] RingCounter,
  input  Halt,
  output HaltSignal
);

  and and_1 (HaltSignal, Halt, RingCounter[3]);
endmodule

module SkipcondInstruction (
  input  [7:0] RingCounter,
  input  Skipcond,
  input  [15:0] IR,
  input  [15:0] AC,
  output IncPC,
  output Cr
);

  wire and_1_out, and_2_out, and_3_out, comparator_1_eq, comparator_1_gt, comparator_1_lt, not_1_out,
       not_2_out, or_1_out;

  not not_1 (not_1_out, IR[10]);
  not not_2 (not_2_out, IR[11]);
  Comparator #(.width(16)) comparator_1 (
    .a(AC), .b({16{1'b0}}), .gt(comparator_1_gt), .eq(comparator_1_eq), .lt(comparator_1_lt));
  and and_1 (and_1_out, not_1_out, not_2_out, comparator_1_lt);
  and and_2 (and_2_out, IR[10], not_2_out, comparator_1_eq);
  and and_3 (and_3_out, IR[10], IR[11], comparator_1_gt);
  or or_1 (or_1_out, and_1_out, and_2_out, and_3_out);
  and and_4 (Cr, RingCounter[3], Skipcond, or_1_out);

  assign IncPC = Cr;
endmodule

module JumpInstruction (
  input  [7:0] RingCounter,
  input  Jump,
  output P0,
  output P1,
  output P2,
  output P4,
  output Cr
);

  and and_1 (Cr, Jump, RingCounter[3]);

  assign P0 = Cr;
  assign P1 = Cr;
  assign P2 = Cr;
  assign P4 = Cr;
endmodule

module ClearInstruction (
  input  [7:0] RingCounter,
  input  Clear,
  output ClearSignal
);

  and and_1 (ClearSignal, Clear, RingCounter[3]);
endmodule

module RingCounter (
  input  Clk,
  input  Cr,
  output T0,
  output T1,
  output T2,
  output T3,
  output T4,
  output T5,
  output T6,
  output T7
);

  nor nor_1 (T0, T7, T6, T5, T4, T3, T2, T1);
  D_Flip_Flop #(.trigger("falling")) d_ff_1 (.D(T0), .clk(Clk), .Q(T1), .reset(Cr));  // open: Qn, preset
  D_Flip_Flop d_ff_2 (.clk(Clk));  // open: D, Q, Qn, preset, reset
  D_Flip_Flop #(.trigger("falling")) d_ff_3 (.D(T1), .clk(Clk), .Q(T2), .reset(Cr));  // open: Qn, preset
  D_Flip_Flop #(.trigger("falling")) d_ff_4 (.D(T2), .clk(Clk), .Q(T3), .reset(Cr));  // open: Qn, preset
  D_Flip_Flop #(.trigger("falling")) d_ff_5 (.D(T3), .clk(Clk), .Q(T4), .reset(Cr));  // open: Qn, preset
  D_Flip_Flop #(.trigger("falling")) d_ff_6 (.D(T4), .clk(Clk), .Q(T5), .reset(Cr));  // open: Qn, preset
  D_Flip_Flop #(.trigger("falling")) d_ff_7 (.D(T5), .clk(Clk), .Q(T6), .reset(Cr));  // open: Qn, preset
  D_Flip_Flop #(.trigger("falling")) d_ff_8 (.D(T6), .clk(Clk), .Q(T7), .reset(Cr));  // open: Qn, preset
endmodule
